# Fritzing sketch ControlUnitConnected (saved by Fritzing 0.9.3b)
circuit board: 10cm x 6cm
breadboards: 2

parts:
  Part1 = Adafruit Feather 32u4 RFM69 433/900MHz [part_number="Adafruit #3076 and #3077"]
  Part3 = Adafruit Bluefruit LE SPI Friend [part_number="Adafruit #2633"]
  Part4 = MCP9808 High Accuracy I2C Temperature Sensor [part_number=1782]
  Q1 = NPN-Transistor [package="TO92 [THT]"]
  Q2 = NPN-Transistor [package="TO92 [THT]"]
  R1 = Resistor [tolerance=±5% resistance=1k package="0603 [SMD]"]
  R2 = Resistor [tolerance=±5% resistance=1k package="0603 [SMD]"]
  J1 = Screw terminal - 2 pins [package=THT]
  J2 = Screw terminal - 2 pins [package=THT]
  Part2 = Adafruit PCF8523 RTC [part_number="Adafruit #3295"]

nets (from the schematic view):
  N1: Part1.0, Part1.MISO, Part1.MOSI, Part1.SCK, Part3.SCK, Part3.MISO, Part3.MOSI
  N2: Part1.VBUS, J1.pin1, J2.pin1
  N3: Part1.12, R2.Pin_1
  N4: Part1.11, R1.Pin_1
  N5: Part1.3, Part4.SCL, Part2.SCL
  N6: Part1.2, Part4.SDA, Part2.SDA
  GND: Part3.GND, Part4.GND, Q1.E, Q2.E
  VIN: Part3.VIN, Part2.VCC
  N7: Q1.B, R2.Pin_0
  N8: Q1.C, J2.pin2
  N9: Q2.B, R1.Pin_0
  N10: Q2.C, J1.pin2

custom parts:
  Adafruit Feather 32u4 RFM69 433/900MHz: This is the Adafruit Feather 32u4 Radio (RFM69HCW) - our take on an microcontroller packet radio transceiver with built in USB and battery charging. Its an Adafruit Feather 32u4 with a 433 or 900 MHz radio module cooked in! Great for making wireless networks that can go further than 2.4GHz 802.15.4 and similar, are more flexible than Bluetooth LE and without the high power requirements of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
  Adafruit Bluefruit LE SPI Friend: The Bluefruit LE SPI Friend makes it easy to add Bluetooth Low Energy connectivity to anything with 4 or 5 GPIO pins. With SPI, you don't have to worry about baud rates, flow control, or giving up a hardware UART port. Connect to your Arduino or other microcontroller using the common four-pin SPI interface (MISO, MOSI, SCK and CS) plus a 5th GPIO pin for interrupts (to let the Arduino know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
  MCP9808 High Accuracy I2C Temperature Sensor: This I2C digital temperature sensor is one of the more accurate/precise we've ever seen, with a typical accuracy of ±0.25°C over the sensor's -40°C to +125°C range and precision of +0.0625°C. They work great with any microcontroller using standard i2c. There are 3 address pins so you can connect up to 8 to a single I2C bus without address collisions. Best of all, a wide voltage range makes is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
  Adafruit PCF8523 RTC: This is a great battery-backed real time clock (RTC) that allows your microcontroller project to keep track of time even if it is reprogrammed, or if the power is lost. Perfect for datalogging, clock-building, time stamping, timers and alarms, etc. Equipped with PCF8523 RTC - it can run from 3.3V or 5V power & logic! Works great with an Arduino using our RTC library, with CircuitPython or with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
