# Fritzing sketch ControlUnitConnectedv2 (saved by Fritzing 0.9.3b)
circuit board: 8.46667cm x 5.64444cm
breadboards: 1

parts:
  Control_Unit_Feather = Adafruit Feather 32u4 RFM69 433/900MHz [part_number="Adafruit #3076 and #3077"]
  RTC = Adafruit PCF8523 RTC [part_number="Adafruit #3295"]
  Air_Temp_Sensor = MCP9808 High Accuracy I2C Temperature Sensor [part_number=1782]
  Bluetooth_Module = Adafruit Bluefruit LE SPI Friend [part_number="Adafruit #2633"]
  Pump/Heater_Terminal = Screw terminal - 2 pins [package=THT]
  Pump_BJT = TRANSISTOR_NPN [package=to-92-ammo]
  Heater_BJT = TRANSISTOR_NPN [package=to-92-ammo]
  Pump_R = Resistor [tolerance=±5% resistance=1k package="2512 [SMD]"]
  Heater_R = Resistor [tolerance=±5% resistance=1k package="2512 [SMD]"]

nets:
  N1: Control_Unit_Feather.MISO, Bluetooth_Module.MISO
  N2: Control_Unit_Feather.MOSI, Bluetooth_Module.MOSI
  N3: Control_Unit_Feather.SCK, Bluetooth_Module.SCK
  GND: Control_Unit_Feather.GND, RTC.GND, Air_Temp_Sensor.GND, Bluetooth_Module.GND, Pump_BJT.E, Heater_BJT.E
  +3V3: Control_Unit_Feather.+3V3, RTC.VCC, Air_Temp_Sensor.VDD, Bluetooth_Module.VIN
  N4: Control_Unit_Feather.12, Heater_R.Pin_0
  N5: Control_Unit_Feather.11, Pump_R.Pin_0
  N6: Control_Unit_Feather.10, Bluetooth_Module.CS
  N7: Control_Unit_Feather.9, Bluetooth_Module.IRQ
  N8: Control_Unit_Feather.6, Bluetooth_Module.RST
  N9: RTC.SCL, Air_Temp_Sensor.SCL
  N10: RTC.SDA, Air_Temp_Sensor.SDA
  N11: Pump/Heater_Terminal.pin1, Heater_BJT.C
  N12: Pump/Heater_Terminal.pin2, Pump_BJT.C
  N13: Pump_BJT.B, Pump_R.Pin_1
  N14: Heater_BJT.B, Heater_R.Pin_1

custom parts:
  Adafruit Feather 32u4 RFM69 433/900MHz: This is the Adafruit Feather 32u4 Radio (RFM69HCW) - our take on an microcontroller packet radio transceiver with built in USB and battery charging. Its an Adafruit Feather 32u4 with a 433 or 900 MHz radio module cooked in! Great for making wireless networks that can go further than 2.4GHz 802.15.4 and similar, are more flexible than Bluetooth LE and without the high power requirements of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
  Adafruit PCF8523 RTC: This is a great battery-backed real time clock (RTC) that allows your microcontroller project to keep track of time even if it is reprogrammed, or if the power is lost. Perfect for datalogging, clock-building, time stamping, timers and alarms, etc. Equipped with PCF8523 RTC - it can run from 3.3V or 5V power & logic! Works great with an Arduino using our RTC library, with CircuitPython or with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
  MCP9808 High Accuracy I2C Temperature Sensor: This I2C digital temperature sensor is one of the more accurate/precise we've ever seen, with a typical accuracy of ±0.25°C over the sensor's -40°C to +125°C range and precision of +0.0625°C. They work great with any microcontroller using standard i2c. There are 3 address pins so you can connect up to 8 to a single I2C bus without address collisions. Best of all, a wide voltage range makes is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
  Adafruit Bluefruit LE SPI Friend: The Bluefruit LE SPI Friend makes it easy to add Bluetooth Low Energy connectivity to anything with 4 or 5 GPIO pins. With SPI, you don't have to worry about baud rates, flow control, or giving up a hardware UART port. Connect to your Arduino or other microcontroller using the common four-pin SPI interface (MISO, MOSI, SCK and CS) plus a 5th GPIO pin for interrupts (to let the Arduino know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
