# Fritzing sketch SensorUnitConnected (saved by Fritzing 0.9.3b)
circuit board: 4cm x 6cm
breadboards: 1

parts:
  Part1 = Adafruit Feather 32u4 RFM69 433/900MHz [part_number="Adafruit #3076 and #3077"]
  DS1 = DS18B20 1-Wire Temperature Sensor Probe Cable
  R1 = Resistor [tolerance=±5% resistance=4.7k package=THT]

nets:
  GND: Part1.GND, DS1.GND, R1.Pin_0
  +3V3: Part1.+3V3, DS1.VDD
  N1: Part1.13, R1.Pin_1

custom parts:
  Adafruit Feather 32u4 RFM69 433/900MHz: This is the Adafruit Feather 32u4 Radio (RFM69HCW) - our take on an microcontroller packet radio transceiver with built in USB and battery charging. Its an Adafruit Feather 32u4 with a 433 or 900 MHz radio module cooked in! Great for making wireless networks that can go further than 2.4GHz 802.15.4 and similar, are more flexible than Bluetooth LE and without the high power requirements of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
