# Fritzing sketch SensorUnitConnectedv2 (saved by Fritzing 0.9.3b)
circuit board: 5.3cm x 2.5cm
breadboards: 1

parts:
  Sensor_Unit_Feather = Adafruit Feather 32u4 RFM69 433/900MHz [part_number="Adafruit #3076 and #3077"]
  Water_Temp_Sensor = DS18B20 1-Wire Temperature Sensor [part_number=DS18B20]

nets:
  GND: Sensor_Unit_Feather.GND, Water_Temp_Sensor.GND
  +3V3: Sensor_Unit_Feather.+3V3, Water_Temp_Sensor.VDD
  N1: Sensor_Unit_Feather.13, Water_Temp_Sensor.DQ

custom parts:
  Adafruit Feather 32u4 RFM69 433/900MHz: This is the Adafruit Feather 32u4 Radio (RFM69HCW) - our take on an microcontroller packet radio transceiver with built in USB and battery charging. Its an Adafruit Feather 32u4 with a 433 or 900 MHz radio module cooked in! Great for making wireless networks that can go further than 2.4GHz 802.15.4 and similar, are more flexible than Bluetooth LE and without the high power requirements of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
